// Logisim project Mealy_1101.circ as structural Verilog: 1 circuit, main circuit Mealy_1101
module Mealy_1101 (
  input  in_1,
  output out_2
);

  wire and_1_out, and_2_out, clock_1_out, d_ff_1_q, d_ff_2_q, d_ff_3_q;

  Clock clock_1 (.out(clock_1_out));
  D_Flip_Flop d_ff_1 (.clk(clock_1_out), .D(in_1), .Q(d_ff_1_q), .reset(out_2));  // open: Qn, preset
  and and_1 (and_1_out, d_ff_1_q, in_1);
  D_Flip_Flop d_ff_2 (.clk(clock_1_out), .D(and_1_out), .Q(d_ff_2_q));  // open: Qn, preset, reset
  D_Flip_Flop d_ff_3 (.clk(clock_1_out), .D(d_ff_2_q), .Q(d_ff_3_q));  // open: Qn, preset, reset
  and and_2 (and_2_out, d_ff_3_q, in_1);
  D_Flip_Flop d_ff_4 (.clk(clock_1_out), .D(and_2_out), .Q(out_2));  // open: Qn, preset, reset
endmodule
