// Logisim project Guia_1101.circ as structural Verilog: 1 circuit, main circuit Guia_1101
module Guia_1101 (
  input  clock,
  input  entrada,
  input  CLR,
  output out_4
);

  wire d_ff_1_q, d_ff_2_q, d_ff_3_q, d_ff_4_q, not_1_out;

  D_Flip_Flop d_ff_1 (.clk(clock), .D(entrada), .Q(d_ff_1_q), .reset(CLR));  // open: Qn, preset
  D_Flip_Flop d_ff_2 (.clk(clock), .D(d_ff_1_q), .Q(d_ff_2_q), .reset(CLR));  // open: Qn, preset
  D_Flip_Flop d_ff_3 (.clk(clock), .D(d_ff_2_q), .Q(d_ff_3_q), .reset(CLR));  // open: Qn, preset
  not not_1 (not_1_out, d_ff_2_q);
  D_Flip_Flop d_ff_4 (.clk(clock), .D(d_ff_3_q), .Q(d_ff_4_q), .reset(CLR));  // open: Qn, preset
  and and_1 (out_4, d_ff_4_q, d_ff_3_q, not_1_out, d_ff_1_q);
endmodule
