// Logisim project Guia_1103.circ as structural Verilog: 1 circuit, main circuit Guia_1103
module Guia_1103 (
  input  entrada,
  input  CLR,
  output out_3,
  output out_4
);

  wire clock_out;

  Clock clock (.out(clock_out));
  Guia_1101 guia_1101_1 (.clock(clock_out), .entrada(entrada), .CLR(CLR), .out_4(out_3));
  Guia_1102 guia_1102_1 (.clock(clock_out), .entrada(entrada), .CLR(CLR), .out_4(out_4));
endmodule
