// Logisim project Guia_1104.circ as structural Verilog: 2 circuits, main circuit Guia_1104
module Guia_1104 (
  input  entrada,
  input  CLR,
  output out_3
);

  wire clock_out, d_ff_1_q, d_ff_2_q, d_ff_3_q, gerenciador_de_estados_1_out_5,
       gerenciador_de_estados_1_out_6, gerenciador_de_estados_1_out_7, not_1_out;

  Clock clock (.out(clock_out));
  Gerenciador_de_Estados gerenciador_de_estados_1 (
    .\input (entrada), .estado_bit2(d_ff_3_q), .estado_bit1(d_ff_2_q), .estado_bit0(d_ff_1_q),
    .out_5(gerenciador_de_estados_1_out_5), .out_6(gerenciador_de_estados_1_out_6),
    .out_7(gerenciador_de_estados_1_out_7));
  D_Flip_Flop d_ff_1 (
    .clk(clock_out), .D(gerenciador_de_estados_1_out_7), .Q(d_ff_1_q), .reset(CLR));  // open: Qn, preset
  D_Flip_Flop d_ff_2 (
    .clk(clock_out), .D(gerenciador_de_estados_1_out_6), .Q(d_ff_2_q), .reset(CLR));  // open: Qn, preset
  D_Flip_Flop d_ff_3 (
    .clk(clock_out), .D(gerenciador_de_estados_1_out_5), .Q(d_ff_3_q), .reset(CLR));  // open: Qn, preset
  not not_1 (not_1_out, d_ff_3_q);
  and and_1 (out_3, entrada, d_ff_2_q, not_1_out);
endmodule

module Gerenciador_de_Estados (
  input  \input ,
  input  estado_bit2,
  input  estado_bit1,
  input  estado_bit0,
  output out_5,
  output out_6,
  output out_7
);

  wire not_1_out, not_2_out, not_3_out, not_4_out, not_5_out, not_6_out;

  not not_1 (not_1_out, \input );
  not not_2 (not_2_out, estado_bit2);
  not not_3 (not_3_out, estado_bit2);
  not not_4 (not_4_out, estado_bit1);
  not not_5 (not_5_out, \input );
  not not_6 (not_6_out, estado_bit1);
  and and_1 (out_5, not_1_out, not_2_out);
  and and_2 (out_6, not_3_out, not_4_out, estado_bit0);
  and and_3 (out_7, not_5_out, not_6_out);
endmodule
