// Logisim project Guia_1106.circ as structural Verilog: 1 circuit, main circuit Guia_1106
module Guia_1106 (
  input  Entrada,
  input  CLR,
  output out_3
);

  wire clock_out, d_ff_1_q, d_ff_2_q, d_ff_3_q, d_ff_4_q, d_ff_5_q, d_ff_6_q, not_1_out, not_2_out, not_3_out;

  Clock clock (.out(clock_out));
  D_Flip_Flop d_ff_1 (.clk(clock_out), .D(Entrada), .Q(d_ff_1_q), .reset(CLR));  // open: Qn, preset
  D_Flip_Flop d_ff_2 (.clk(clock_out), .D(d_ff_1_q), .Q(d_ff_2_q), .reset(CLR));  // open: Qn, preset
  D_Flip_Flop d_ff_3 (.clk(clock_out), .D(d_ff_2_q), .Q(d_ff_3_q), .reset(CLR));  // open: Qn, preset
  D_Flip_Flop d_ff_4 (.clk(clock_out), .D(d_ff_3_q), .Q(d_ff_4_q), .reset(CLR));  // open: Qn, preset
  D_Flip_Flop d_ff_5 (.clk(clock_out), .D(d_ff_4_q), .Q(d_ff_5_q), .reset(CLR));  // open: Qn, preset
  D_Flip_Flop d_ff_6 (.clk(clock_out), .D(d_ff_5_q), .Q(d_ff_6_q), .reset(CLR));  // open: Qn, preset
  not not_1 (not_1_out, d_ff_4_q);
  not not_2 (not_2_out, d_ff_6_q);
  not not_3 (not_3_out, d_ff_3_q);
  and and_1 (out_3, not_2_out, d_ff_5_q, not_1_out, not_3_out, d_ff_2_q);
endmodule
