// Logisim project Guia_13.circ as structural Verilog: 5 circuits, main circuit Guia_1301
module Guia_1301 (
  input  entrada,
  input  CLR,
  output out_3,
  output out_4,
  output out_5,
  output out_6,
  output out_7
);

  wire clock_out;

  Clock clock (.out(clock_out));
  J_K_Flip_Flop j_k_ff_1 (.J(entrada), .clk(out_4), .K(entrada), .Qn(out_3), .reset(CLR));  // open: Q, preset
  J_K_Flip_Flop j_k_ff_2 (.J(entrada), .clk(out_5), .K(entrada), .Qn(out_4), .reset(CLR));  // open: Q, preset
  J_K_Flip_Flop j_k_ff_3 (.J(entrada), .clk(out_6), .K(entrada), .Qn(out_5), .reset(CLR));  // open: Q, preset
  J_K_Flip_Flop j_k_ff_4 (.J(entrada), .clk(out_7), .K(entrada), .Qn(out_6), .reset(CLR));  // open: Q, preset
  J_K_Flip_Flop j_k_ff_5 (.J(entrada), .clk(clock_out), .K(entrada), .Qn(out_7), .reset(CLR));  // open: Q, preset
endmodule

module Guia_1302 (
  input  entrada,
  input  CLR,
  output out_3,
  output out_4,
  output out_5,
  output out_6,
  output out_7
);

  wire clock_out, j_k_ff_2_qn, j_k_ff_3_qn, j_k_ff_4_qn, j_k_ff_5_qn;

  Clock clock (.out(clock_out));
  J_K_Flip_Flop j_k_ff_1 (.J(entrada), .clk(j_k_ff_2_qn), .K(entrada), .Q(out_3), .reset(CLR));  // open: Qn, preset
  J_K_Flip_Flop j_k_ff_2 (
    .J(entrada), .clk(j_k_ff_3_qn), .K(entrada), .Q(out_4), .Qn(j_k_ff_2_qn), .reset(CLR));  // open: preset
  J_K_Flip_Flop j_k_ff_3 (
    .J(entrada), .clk(j_k_ff_4_qn), .K(entrada), .Q(out_5), .Qn(j_k_ff_3_qn), .reset(CLR));  // open: preset
  J_K_Flip_Flop j_k_ff_4 (
    .J(entrada), .clk(j_k_ff_5_qn), .K(entrada), .Q(out_6), .Qn(j_k_ff_4_qn), .reset(CLR));  // open: preset
  J_K_Flip_Flop j_k_ff_5 (
    .J(entrada), .clk(clock_out), .K(entrada), .Q(out_7), .Qn(j_k_ff_5_qn), .reset(CLR));  // open: preset
endmodule

module Guia_1303 (
  input  entrada,
  input  CLR,
  output [3:0] out_3
);

  wire and_1_out, and_2_out, clock_out, j_k_ff_1_qn, j_k_ff_2_qn, j_k_ff_3_qn, not_1_out, not_2_out;

  Clock clock (.out(clock_out));
  and and_1 (and_1_out, CLR, not_1_out);
  not not_1 (not_1_out, and_2_out);
  and and_2 (and_2_out, out_3[0], out_3[1], not_2_out, out_3[3]);
  J_K_Flip_Flop j_k_ff_1 (
    .J(entrada), .clk(clock_out), .K(entrada), .Q(out_3[0]), .Qn(j_k_ff_1_qn), .reset(and_1_out));  // open: preset
  not not_2 (not_2_out, out_3[2]);
  J_K_Flip_Flop j_k_ff_2 (
    .J(entrada), .clk(j_k_ff_1_qn), .K(entrada), .Q(out_3[1]), .Qn(j_k_ff_2_qn), .reset(and_1_out));  // open: preset
  J_K_Flip_Flop j_k_ff_3 (
    .J(entrada), .clk(j_k_ff_2_qn), .K(entrada), .Q(out_3[2]), .Qn(j_k_ff_3_qn), .reset(and_1_out));  // open: preset
  J_K_Flip_Flop j_k_ff_4 (
    .J(entrada), .clk(j_k_ff_3_qn), .K(entrada), .Q(out_3[3]), .reset(and_1_out));  // open: Qn, preset
endmodule

module Guia_1304 (
  input  entrada,
  input  CLR,
  output [3:0] out_3
);

  wire and_1_out, clock_out, j_k_ff_1_qn, j_k_ff_2_qn, j_k_ff_3_qn, j_k_ff_4_qn, not_1_out, or_1_out;

  Clock clock (.out(clock_out));
  J_K_Flip_Flop j_k_ff_1 (
    .J(entrada), .clk(clock_out), .K(entrada), .Q(out_3[0]), .Qn(j_k_ff_1_qn), .preset(or_1_out), .reset(CLR));
  not not_1 (not_1_out, entrada);
  or or_1 (or_1_out, not_1_out, and_1_out);
  and and_1 (and_1_out, j_k_ff_1_qn, j_k_ff_2_qn, j_k_ff_3_qn, j_k_ff_4_qn);
  J_K_Flip_Flop j_k_ff_2 (
    .J(entrada), .clk(out_3[0]), .K(entrada), .Q(out_3[1]), .Qn(j_k_ff_2_qn), .preset(or_1_out), .reset(CLR));
  J_K_Flip_Flop j_k_ff_3 (
    .J(entrada), .clk(out_3[1]), .K(entrada), .Q(out_3[2]), .Qn(j_k_ff_3_qn), .preset(or_1_out), .reset(CLR));
  J_K_Flip_Flop j_k_ff_4 (
    .J(entrada), .clk(out_3[2]), .K(entrada), .Q(out_3[3]), .Qn(j_k_ff_4_qn), .preset(or_1_out), .reset(CLR));
endmodule

module Guia_1305 (
  input  data,
  input  clear,
  output [2:0] out_3
);

  wire and_1_out, clock_out;

  Clock clock (.out(clock_out));
  T_Flip_Flop t_ff_1 (.clk(clock_out), .T(data), .Q(out_3[2]), .reset(clear));  // open: Qn, preset
  T_Flip_Flop t_ff_2 (.clk(clock_out), .T(out_3[2]), .Q(out_3[1]), .reset(clear));  // open: Qn, preset
  and and_1 (and_1_out, out_3[1], out_3[2]);
  T_Flip_Flop t_ff_3 (.clk(clock_out), .T(and_1_out), .Q(out_3[0]), .reset(clear));  // open: Qn, preset
endmodule
