// Logisim project Guia_05.circ as structural Verilog
module Guia_0501 (
  input  a,
  input  b,
  output s
);

  nor nor_1 (s, a, b);
endmodule

module Guia_0502 (
  input  a,
  input  b,
  output s
);

  wire nand_1_out;

  nand nand_1 (nand_1_out, a, a);
  nand nand_2 (s, nand_1_out, b);
endmodule

module Guia_0503 (
  input  a,
  input  b,
  output s
);

  wire nor_1_out, nor_2_out, nor_3_out;

  nor nor_1 (nor_1_out, a, a);
  nor nor_2 (nor_2_out, b, b);
  nor nor_3 (nor_3_out, nor_1_out, nor_2_out);
  nor nor_4 (s, nor_3_out, nor_3_out);
endmodule

module Guia_0504 (
  input  a,
  input  b,
  output s
);

  wire nand_1_out;

  nand nand_1 (nand_1_out, a, a);
  nand nand_2 (s, nand_1_out, b);
endmodule

module Guia_0505 (
  input  a,
  input  b,
  output s
);

  wire nor_1_out, nor_2_out, nor_3_out;

  nor nor_1 (nor_1_out, a, nor_2_out);
  nor nor_2 (nor_2_out, a, b);
  nor nor_3 (nor_3_out, nor_2_out, b);
  nor nor_4 (s, nor_1_out, nor_3_out);
endmodule

module Guia_0506 (
  input  a,
  input  b,
  output s
);

  wire nand_1_out, nand_2_out, nand_3_out, nand_4_out;

  nand nand_1 (nand_1_out, a, a);
  nand nand_2 (nand_2_out, b, b);
  nand nand_3 (nand_3_out, nand_1_out, b);
  nand nand_4 (nand_4_out, a, nand_2_out);
  nand nand_5 (s, nand_3_out, nand_4_out);
endmodule

module Guia_0508 (
  input  a,
  input  b,
  output s
);

  wire nand_1_out;

  nand nand_1 (nand_1_out, b, b);
  nand nand_2 (s, a, nand_1_out);
endmodule
