// Logisim project Guia_06.circ as structural Verilog
module Guia_0606 (
  input  x,
  input  y,
  input  w,
  input  z,
  output out_5
);

  wire not_1_out, not_2_out, not_3_out, or_1_out;

  not not_1 (not_1_out, y);
  not not_2 (not_2_out, w);
  not not_3 (not_3_out, z);
  and and_1 (out_5, x, or_1_out);
  or or_1 (or_1_out, not_1_out, not_2_out, not_3_out);
endmodule

module Guia_0605 (
  input  x,
  input  y,
  input  z,
  output out_4
);

  wire and_1_out, and_2_out, not_1_out, not_2_out;

  not not_1 (not_1_out, y);
  not not_2 (not_2_out, z);
  and and_1 (and_1_out, x, not_1_out);
  and and_2 (and_2_out, not_2_out, x);
  or or_1 (out_4, and_1_out, and_2_out);
endmodule

module Guia_0601a (
  input  x,
  input  y,
  input  z,
  output out_4
);

  wire and_1_out, and_2_out, not_1_out;

  not not_1 (not_1_out, x);
  and and_1 (and_1_out, not_1_out, z);
  and and_2 (and_2_out, y, z);
  or or_1 (out_4, and_1_out, and_2_out);
endmodule

module Guia_0601b (
  input  x,
  input  y,
  input  z,
  output out_4
);

  wire and_1_out, and_2_out, not_1_out, not_2_out, not_3_out;

  not not_1 (not_1_out, x);
  not not_2 (not_2_out, z);
  not not_3 (not_3_out, z);
  and and_1 (and_1_out, not_1_out, not_2_out);
  and and_2 (and_2_out, y, not_3_out);
  or or_1 (out_4, and_1_out, and_2_out);
endmodule

module Guia_0601c (
  input  x,
  input  y,
  input  z,
  output out_4
);

  wire and_1_out, and_2_out, not_1_out, not_2_out;

  not not_1 (not_1_out, z);
  not not_2 (not_2_out, y);
  and and_1 (and_1_out, y, not_1_out);
  and and_2 (and_2_out, x, not_2_out);
  or or_1 (out_4, and_1_out, and_2_out);
endmodule

module Guia_0601d (
  input  x,
  input  y,
  input  z,
  output out_4
);

  wire and_1_out, and_2_out, not_1_out, not_2_out;

  not not_1 (not_1_out, y);
  not not_2 (not_2_out, x);
  and and_1 (and_1_out, not_1_out, z);
  and and_2 (and_2_out, not_2_out, y);
  or or_1 (out_4, and_1_out, and_2_out);
endmodule

module Guia_0601e (
  input  x,
  input  y,
  input  z,
  output out_4
);

  wire and_1_out, and_2_out, not_1_out, not_2_out;

  not not_1 (not_1_out, y);
  not not_2 (not_2_out, z);
  and and_1 (and_1_out, not_1_out, not_2_out);
  and and_2 (and_2_out, x, z);
  or or_1 (out_4, and_1_out, and_2_out);
endmodule

module Guia_0602a (
  input  x,
  input  y,
  input  z,
  output out_4
);

  wire not_1_out, not_2_out, not_3_out, or_1_out, or_2_out;

  not not_1 (not_1_out, x);
  not not_2 (not_2_out, x);
  not not_3 (not_3_out, z);
  or or_1 (or_1_out, not_1_out, y);
  or or_2 (or_2_out, not_2_out, not_3_out);
  and and_1 (out_4, or_1_out, or_2_out);
endmodule

module Guia_0602b (
  input  x,
  input  y,
  input  z,
  output out_4
);

  wire not_1_out, not_2_out, not_3_out, or_1_out, or_2_out;

  not not_1 (not_1_out, y);
  or or_1 (or_1_out, not_1_out, z);
  not not_2 (not_2_out, x);
  or or_2 (or_2_out, not_2_out, y, not_3_out);
  not not_3 (not_3_out, z);
  and and_1 (out_4, or_1_out, or_2_out);
endmodule

module Guia_0602c (
  input  x,
  input  y,
  input  z,
  output out_4
);

  wire not_1_out, not_2_out, or_1_out, or_2_out;

  not not_1 (not_1_out, z);
  not not_2 (not_2_out, y);
  or or_1 (or_1_out, y, not_1_out);
  or or_2 (or_2_out, x, not_2_out);
  and and_1 (out_4, or_1_out, or_2_out);
endmodule

module Guia_0602d (
  input  x,
  input  y,
  input  z,
  output out_4
);

  wire not_1_out, not_2_out, not_3_out, or_1_out, or_2_out;

  or or_1 (or_1_out, x, not_1_out);
  not not_1 (not_1_out, y);
  not not_2 (not_2_out, x);
  or or_2 (or_2_out, not_2_out, not_3_out);
  not not_3 (not_3_out, z);
  and and_1 (out_4, or_1_out, or_2_out);
endmodule

module Guia_0602e (
  input  x,
  input  y,
  input  z,
  output out_4
);

  wire not_1_out, not_2_out, not_3_out, not_4_out, or_1_out, or_2_out, or_3_out;

  not not_1 (not_1_out, y);
  or or_1 (or_1_out, not_1_out, z);
  not not_2 (not_2_out, x);
  or or_2 (or_2_out, not_2_out, z);
  not not_3 (not_3_out, x);
  or or_3 (or_3_out, not_3_out, not_4_out);
  not not_4 (not_4_out, y);
  and and_1 (out_4, or_1_out, or_2_out, or_3_out);
endmodule

module Guia_0603a (
  input  x,
  input  y,
  input  w,
  input  z,
  output out_5
);

  wire and_1_out, and_2_out, and_3_out, and_4_out, not_1_out, not_2_out, not_3_out, not_4_out, not_5_out,
       not_6_out, not_7_out;

  not not_1 (not_1_out, x);
  not not_2 (not_2_out, w);
  not not_3 (not_3_out, y);
  not not_4 (not_4_out, z);
  not not_5 (not_5_out, w);
  not not_6 (not_6_out, y);
  not not_7 (not_7_out, z);
  and and_1 (and_1_out, not_1_out, not_2_out, z);
  and and_2 (and_2_out, not_3_out, w, not_4_out);
  and and_3 (and_3_out, y, not_5_out, z);
  and and_4 (and_4_out, x, not_6_out, not_7_out);
  or or_1 (out_5, and_1_out, and_2_out, and_3_out, and_4_out);
endmodule

module Guia_0603b (
  input  x,
  input  y,
  input  w,
  input  z,
  output out_5
);

  wire and_1_out, and_2_out, and_3_out, and_4_out, not_1_out, not_2_out, not_3_out, not_4_out, not_5_out,
       not_6_out;

  not not_1 (not_1_out, x);
  and and_1 (and_1_out, not_1_out, z);
  not not_2 (not_2_out, x);
  not not_3 (not_3_out, y);
  and and_2 (and_2_out, not_2_out, not_3_out, not_4_out);
  not not_4 (not_4_out, w);
  not not_5 (not_5_out, y);
  and and_3 (and_3_out, not_5_out, w, z);
  not not_6 (not_6_out, w);
  and and_4 (and_4_out, y, not_6_out, z);
  or or_1 (out_5, and_1_out, and_2_out, and_3_out, and_4_out);
endmodule

module Guia_0603c (
  input  x,
  input  y,
  input  w,
  input  z,
  output out_5
);

  wire and_1_out, and_2_out, and_3_out, and_4_out, not_1_out, not_2_out, not_3_out, not_4_out, not_5_out,
       not_6_out;

  not not_1 (not_1_out, x);
  not not_2 (not_2_out, y);
  and and_1 (and_1_out, not_1_out, not_2_out, not_3_out);
  not not_3 (not_3_out, w);
  not not_4 (not_4_out, x);
  and and_2 (and_2_out, not_4_out, w, not_5_out);
  not not_5 (not_5_out, z);
  and and_3 (and_3_out, y, w, z);
  not not_6 (not_6_out, y);
  and and_4 (and_4_out, x, not_6_out, z);
  or or_1 (out_5, and_1_out, and_2_out, and_3_out, and_4_out);
endmodule

module Guia_0603d (
  input  x,
  input  y,
  input  w,
  input  z,
  output out_5
);

  wire and_1_out, and_2_out, and_3_out, and_4_out, and_5_out, not_1_out, not_2_out, not_3_out, not_4_out,
       not_5_out, not_6_out, not_7_out, not_8_out;

  not not_1 (not_1_out, x);
  not not_2 (not_2_out, w);
  not not_3 (not_3_out, x);
  not not_4 (not_4_out, w);
  not not_5 (not_5_out, x);
  not not_6 (not_6_out, y);
  not not_7 (not_7_out, z);
  not not_8 (not_8_out, z);
  and and_1 (and_1_out, not_1_out, y, not_2_out);
  and and_2 (and_2_out, not_3_out, y, y);
  and and_3 (and_3_out, x, not_4_out, z);
  and and_4 (and_4_out, not_5_out, not_6_out, w, not_7_out);
  and and_5 (and_5_out, x, y, w, not_8_out);
  or or_1 (out_5, and_1_out, and_2_out, and_3_out, and_4_out, and_5_out);
endmodule

module Guia_0603e (
  input  x,
  input  y,
  input  w,
  input  z,
  output out_5
);

  wire and_1_out, and_2_out, and_3_out, not_1_out, not_2_out, not_3_out, not_4_out;

  not not_1 (not_1_out, y);
  and and_1 (and_1_out, not_1_out, not_2_out);
  not not_2 (not_2_out, w);
  not not_3 (not_3_out, x);
  and and_2 (and_2_out, not_3_out, w, z);
  and and_3 (and_3_out, x, y, not_4_out);
  not not_4 (not_4_out, z);
  or or_1 (out_5, and_1_out, and_2_out, and_3_out);
endmodule

module Guia_0604a (
  input  x,
  input  y,
  input  w,
  input  z,
  output out_5
);

  wire not_1_out, not_2_out, not_3_out, not_4_out, not_5_out, not_6_out, or_1_out, or_2_out, or_3_out;

  not not_1 (not_1_out, w);
  or or_1 (or_1_out, x, not_1_out, z);
  not not_2 (not_2_out, y);
  or or_2 (or_2_out, x, not_2_out, not_3_out);
  not not_3 (not_3_out, w);
  not not_4 (not_4_out, x);
  not not_5 (not_5_out, y);
  or or_3 (or_3_out, not_4_out, not_5_out, w, not_6_out);
  not not_6 (not_6_out, z);
  and and_1 (out_5, or_1_out, or_2_out, or_3_out);
endmodule

module Guia_0604b (
  input  x,
  input  y,
  input  w,
  input  z,
  output out_5
);

  wire not_1_out, not_2_out, not_3_out, not_4_out, not_5_out, not_6_out, or_1_out, or_2_out, or_3_out;

  not not_1 (not_1_out, y);
  not not_2 (not_2_out, w);
  or or_1 (or_1_out, not_1_out, not_2_out, not_3_out);
  not not_3 (not_3_out, z);
  not not_4 (not_4_out, x);
  or or_2 (or_2_out, not_4_out, y, not_5_out);
  not not_5 (not_5_out, z);
  not not_6 (not_6_out, y);
  or or_3 (or_3_out, x, not_6_out, w, z);
  and and_1 (out_5, or_1_out, or_2_out, or_3_out);
endmodule

module Guia_0604c (
  input  x,
  input  y,
  input  w,
  input  z,
  output out_5
);

  wire not_1_out, not_2_out, not_3_out, not_4_out, not_5_out, or_1_out, or_2_out, or_3_out;

  not not_1 (not_1_out, y);
  or or_1 (or_1_out, not_1_out, w, z);
  not not_2 (not_2_out, x);
  or or_2 (or_2_out, not_2_out, w, z);
  not not_3 (not_3_out, x);
  not not_4 (not_4_out, y);
  or or_3 (or_3_out, not_3_out, not_4_out, not_5_out);
  not not_5 (not_5_out, z);
  and and_1 (out_5, or_1_out, or_2_out, or_3_out);
endmodule

module Guia_0604d (
  input  x,
  input  y,
  input  w,
  input  z,
  output out_5
);

  wire not_1_out, not_2_out, not_3_out, not_4_out, not_5_out, not_6_out, or_1_out, or_2_out, or_3_out;

  or or_1 (or_1_out, x, w, not_1_out);
  not not_1 (not_1_out, z);
  not not_2 (not_2_out, y);
  or or_2 (or_2_out, not_2_out, not_3_out, z);
  not not_3 (not_3_out, w);
  not not_4 (not_4_out, x);
  not not_5 (not_5_out, y);
  or or_3 (or_3_out, not_4_out, not_5_out, not_6_out);
  not not_6 (not_6_out, z);
  and and_1 (out_5, or_1_out, or_2_out, or_3_out);
endmodule

module Guia_0604e (
  input  x,
  input  y,
  input  w,
  input  z,
  output out_5
);

  wire not_1_out, not_2_out, not_3_out, not_4_out, not_5_out, not_6_out, or_1_out, or_2_out, or_3_out;

  not not_1 (not_1_out, w);
  or or_1 (or_1_out, y, not_1_out, not_2_out);
  not not_2 (not_2_out, z);
  not not_3 (not_3_out, y);
  or or_2 (or_2_out, x, not_3_out, not_4_out);
  not not_4 (not_4_out, z);
  not not_5 (not_5_out, y);
  not not_6 (not_6_out, w);
  or or_3 (or_3_out, not_5_out, not_6_out, z);
  and and_1 (out_5, or_1_out, or_2_out, or_3_out);
endmodule
