// Logisim project Guia_07.circ as structural Verilog: 5 circuits, main circuit Guia_0701
module Guia_0701 (
  input  x,
  input  y,
  input  s,
  output z
);

  wire and_1_out, nand_1_out, not_1_out;

  not not_1 (not_1_out, s);
  nand nand_1 (nand_1_out, x, s);
  and and_1 (and_1_out, not_1_out, y);
  or or_1 (z, nand_1_out, and_1_out);
endmodule

module Guia_0702 (
  input  x,
  input  y,
  input  s,
  output z
);

  wire nor_1_out, not_1_out, or_1_out;

  not not_1 (not_1_out, s);
  nor nor_1 (nor_1_out, x, s);
  or or_1 (or_1_out, not_1_out, y);
  or or_2 (z, nor_1_out, or_1_out);
endmodule

module Guia_0703 (
  input  x,
  input  y,
  input  s1,
  input  s2,
  output z
);

  wire and_1_out, and_2_out, and_3_out, nand_1_out, nor_1_out, not_1_out, not_2_out, not_3_out, or_1_out,
       or_2_out, or_3_out;

  not not_1 (not_1_out, s1);
  not not_2 (not_2_out, s1);
  nand nand_1 (nand_1_out, x, s1);
  and and_1 (and_1_out, not_1_out, y);
  nor nor_1 (nor_1_out, x, s1);
  or or_1 (or_1_out, not_2_out, y);
  or or_2 (or_2_out, nand_1_out, and_1_out);
  not not_3 (not_3_out, s2);
  or or_3 (or_3_out, nor_1_out, or_1_out);
  and and_2 (and_2_out, or_2_out, not_3_out);
  and and_3 (and_3_out, or_3_out, s2);
  or or_4 (z, and_2_out, and_3_out);
endmodule

module Guia_0704 (
  input  in_1,
  input  in_2,
  input  in_3,
  input  in_4,
  output out_5
);

  wire and_1_out, and_2_out, and_3_out, and_4_out, nor_1_out, not_1_out, not_2_out, or_1_out, xnor_1_out,
       xor_1_out;

  xor xor_1 (xor_1_out, in_1, in_2);
  xnor xnor_1 (xnor_1_out, in_1, in_2);
  nor nor_1 (nor_1_out, in_1, in_2);
  or or_1 (or_1_out, in_1, in_2);
  not not_1 (not_1_out, in_3);
  not not_2 (not_2_out, in_4);
  and and_1 (and_1_out, xor_1_out, in_3, in_4);
  and and_2 (and_2_out, xnor_1_out, not_1_out, in_4);
  and and_3 (and_3_out, nor_1_out, not_2_out, in_3);
  and and_4 (and_4_out, or_1_out, not_1_out, not_2_out);
  or or_2 (out_5, and_1_out, and_2_out, and_3_out, and_4_out);
endmodule

module Guia_0705 (
  input  in_1,
  input  in_2,
  input  in_3,
  input  in_4,
  input  in_5,
  output out_6
);

  wire and_1_out, and_2_out, and_3_out, and_4_out, and_5_out, and_6_out, and_7_out, and_8_out, nand_1_out,
       nor_1_out, not_1_out, not_2_out, not_3_out, not_4_out, or_1_out, or_2_out, or_3_out, or_4_out,
       xnor_1_out, xor_1_out;

  and and_1 (and_1_out, in_1, in_2);
  or or_1 (or_1_out, in_1, in_2);
  not not_1 (not_1_out, or_2_out);
  or or_2 (or_2_out, in_1, in_2);
  nand nand_1 (nand_1_out, in_1, in_2);
  nor nor_1 (nor_1_out, in_1, in_2);
  xor xor_1 (xor_1_out, in_1, in_2);
  xnor xnor_1 (xnor_1_out, in_1, in_2);
  not not_2 (not_2_out, in_3);
  not not_3 (not_3_out, in_5);
  not not_4 (not_4_out, in_4);
  and and_2 (and_2_out, and_1_out, not_2_out, not_4_out, not_3_out);
  and and_3 (and_3_out, or_1_out, not_2_out, not_4_out, in_5);
  and and_4 (and_4_out, not_1_out, not_2_out, in_4, not_3_out);
  and and_5 (and_5_out, nand_1_out, not_2_out, in_4, in_5);
  and and_6 (and_6_out, nor_1_out, in_3, not_4_out, not_3_out);
  and and_7 (and_7_out, xor_1_out, in_3, not_4_out, in_5);
  and and_8 (and_8_out, xnor_1_out, in_3, in_3, in_4);
  or or_3 (or_3_out, and_2_out, and_3_out, and_4_out);
  or or_4 (or_4_out, and_5_out, and_6_out, and_7_out, and_8_out);
  or or_5 (out_6, or_3_out, or_4_out);
endmodule
