// Logisim project Guia_08.circ as structural Verilog: 10 circuits, main circuit Guia_0801meiosomador
module Guia_0801meiosomador (
  input  in_1,
  input  in_2,
  output out_3,
  output out_4
);

  wire and_1_out, and_2_out, and_3_out, xor_2_out;

  xor xor_1 (out_4, xor_2_out, 1'b0);
  or or_1 (out_3, and_1_out, and_2_out, and_3_out);
  xor xor_2 (xor_2_out, in_1, in_2);
  and and_1 (and_1_out, in_2, 1'b0);
  and and_2 (and_2_out, in_1, 1'b0);
  and and_3 (and_3_out, in_1, in_2);
endmodule

module Guia_0801completo (
  input  in_1,
  input  in_2,
  input  in_3,
  output out_4,
  output out_5
);

  wire and_1_out, and_2_out, and_3_out, xor_2_out;

  xor xor_1 (out_5, xor_2_out, in_3);
  or or_1 (out_4, and_1_out, and_2_out, and_3_out);
  xor xor_2 (xor_2_out, in_1, in_2);
  and and_1 (and_1_out, in_2, in_3);
  and and_2 (and_2_out, in_1, in_3);
  and and_3 (and_3_out, in_1, in_2);
endmodule

module Guia_0801 (
  input  in_1,
  input  in_2,
  input  in_3,
  input  in_4,
  input  in_5,
  input  in_6,
  input  in_7,
  input  in_8,
  input  in_9,
  input  in_10,
  input  in_11,
  input  in_12,
  output out_13,
  output out_14,
  output out_15,
  output out_16,
  output out_17,
  output out_18
);

  wire guia_0801completo_2_out_4, guia_0801completo_3_out_4, guia_0801completo_4_out_4,
       guia_0801completo_5_out_4, guia_0801meiosomador_1_out_3;

  Guia_0801completo guia_0801completo_1 (
    .out_5(out_13), .in_3(guia_0801completo_2_out_4), .in_1(in_1), .in_2(in_7));  // open: out_4
  Guia_0801completo guia_0801completo_2 (
    .out_4(guia_0801completo_2_out_4), .out_5(out_14), .in_3(guia_0801completo_3_out_4), .in_1(in_2),
    .in_2(in_8));
  Guia_0801completo guia_0801completo_3 (
    .out_4(guia_0801completo_3_out_4), .out_5(out_15), .in_3(guia_0801completo_4_out_4), .in_1(in_3),
    .in_2(in_9));
  Guia_0801completo guia_0801completo_4 (
    .out_4(guia_0801completo_4_out_4), .out_5(out_16), .in_3(guia_0801completo_5_out_4), .in_1(in_4),
    .in_2(in_10));
  Guia_0801completo guia_0801completo_5 (
    .out_4(guia_0801completo_5_out_4), .out_5(out_17), .in_3(guia_0801meiosomador_1_out_3), .in_1(in_5),
    .in_2(in_11));
  Guia_0801meiosomador guia_0801meiosomador_1 (
    .out_3(guia_0801meiosomador_1_out_3), .out_4(out_18), .in_1(in_6), .in_2(in_12));
endmodule

module Guia_0802meiosubtrator (
  input  in_1,
  input  in_2,
  output out_3,
  output out_4
);

  wire and_1_out, and_2_out, and_3_out, not_1_out, not_2_out, xor_2_out;

  xor xor_1 (out_4, xor_2_out, 1'b0);
  or or_1 (out_3, and_1_out, and_2_out, and_3_out);
  xor xor_2 (xor_2_out, in_1, in_2);
  and and_1 (and_1_out, in_2, 1'b0);
  not not_1 (not_1_out, in_1);
  and and_2 (and_2_out, not_1_out, 1'b0);
  not not_2 (not_2_out, in_1);
  and and_3 (and_3_out, not_2_out, in_2);
endmodule

module Guia_0802completo (
  input  in_1,
  input  in_2,
  input  in_3,
  output out_4,
  output out_5
);

  wire and_1_out, and_2_out, and_3_out, not_1_out, not_2_out, xor_2_out;

  xor xor_1 (out_5, xor_2_out, in_3);
  or or_1 (out_4, and_1_out, and_2_out, and_3_out);
  xor xor_2 (xor_2_out, in_1, in_2);
  and and_1 (and_1_out, in_2, in_3);
  not not_1 (not_1_out, in_1);
  and and_2 (and_2_out, not_1_out, in_3);
  not not_2 (not_2_out, in_1);
  and and_3 (and_3_out, not_2_out, in_2);
endmodule

module Guia_0802 (
  input  in_1,
  input  in_2,
  input  in_3,
  input  in_4,
  input  in_5,
  input  in_6,
  input  in_7,
  input  in_8,
  input  in_9,
  input  in_10,
  input  in_11,
  input  in_12,
  output out_13,
  output out_14,
  output out_15,
  output out_16,
  output out_17,
  output out_18
);

  wire guia_0802completo_2_out_4, guia_0802completo_3_out_4, guia_0802completo_4_out_4,
       guia_0802completo_5_out_4, guia_0802meiosubtrator_1_out_3;

  Guia_0802completo guia_0802completo_1 (
    .out_5(out_13), .in_3(guia_0802completo_2_out_4), .in_1(in_1), .in_2(in_7));  // open: out_4
  Guia_0802completo guia_0802completo_2 (
    .out_4(guia_0802completo_2_out_4), .out_5(out_14), .in_3(guia_0802completo_3_out_4), .in_1(in_2),
    .in_2(in_8));
  Guia_0802completo guia_0802completo_3 (
    .out_4(guia_0802completo_3_out_4), .out_5(out_15), .in_3(guia_0802completo_4_out_4), .in_1(in_3),
    .in_2(in_9));
  Guia_0802completo guia_0802completo_4 (
    .out_4(guia_0802completo_4_out_4), .out_5(out_16), .in_3(guia_0802completo_5_out_4), .in_1(in_4),
    .in_2(in_10));
  Guia_0802completo guia_0802completo_5 (
    .out_4(guia_0802completo_5_out_4), .out_5(out_17), .in_3(guia_0802meiosubtrator_1_out_3), .in_1(in_5),
    .in_2(in_11));
  Guia_0802meiosubtrator guia_0802meiosubtrator_1 (
    .out_3(guia_0802meiosubtrator_1_out_3), .out_4(out_18), .in_1(in_6), .in_2(in_12));
endmodule

module Guia_0803 (
  input  in_1,
  input  in_2,
  input  in_3,
  input  in_4,
  input  in_5,
  input  in_6,
  input  in_7,
  input  in_8,
  input  in_9,
  input  in_10,
  input  in_11,
  input  in_12,
  output out_13
);

  wire xor_1_out, xor_2_out, xor_3_out, xor_4_out, xor_5_out, xor_6_out;

  xor xor_1 (xor_1_out, in_1, in_2);
  xor xor_2 (xor_2_out, in_3, in_4);
  xor xor_3 (xor_3_out, in_5, in_6);
  xor xor_4 (xor_4_out, in_7, in_8);
  xor xor_5 (xor_5_out, in_9, in_10);
  xor xor_6 (xor_6_out, in_11, in_12);
  nor nor_1 (out_13, xor_1_out, xor_2_out, xor_3_out, xor_4_out, xor_5_out, xor_6_out);
endmodule

module Guia_0804 (
  input  in_1,
  input  in_2,
  input  in_3,
  input  in_4,
  input  in_5,
  input  in_6,
  input  in_7,
  input  in_8,
  input  in_9,
  input  in_10,
  input  in_11,
  input  in_12,
  output out_13
);

  wire xnor_1_out, xnor_2_out, xnor_3_out, xnor_4_out, xnor_5_out, xnor_6_out;

  xnor xnor_1 (xnor_1_out, in_1, in_2);
  xnor xnor_2 (xnor_2_out, in_3, in_4);
  xnor xnor_3 (xnor_3_out, in_5, in_6);
  xnor xnor_4 (xnor_4_out, in_7, in_8);
  xnor xnor_5 (xnor_5_out, in_9, in_10);
  xnor xnor_6 (xnor_6_out, in_11, in_12);
  nand nand_1 (out_13, xnor_1_out, xnor_2_out, xnor_3_out, xnor_4_out, xnor_5_out, xnor_6_out);
endmodule

module Guia_0805_C1 (
  input  in_1,
  input  in_2,
  input  in_3,
  input  in_4,
  input  in_5,
  input  in_6,
  output out_7,
  output out_8,
  output out_9,
  output out_10,
  output out_11,
  output out_12
);

  not not_1 (out_7, in_1);
  not not_2 (out_8, in_2);
  not not_3 (out_9, in_3);
  not not_4 (out_10, in_4);
  not not_5 (out_12, in_6);
  not not_6 (out_11, in_5);
endmodule

module Guia_0805 (
  input  in_1,
  input  in_2,
  input  in_3,
  input  in_4,
  input  in_5,
  input  in_6,
  input  in_7,
  input  in_8,
  input  in_9,
  input  in_10,
  input  in_11,
  input  in_12,
  output out_13,
  output out_14,
  output out_15,
  output out_16,
  output out_17,
  output out_18
);

  wire guia_0801completo_2_out_4, guia_0801completo_3_out_4, guia_0801completo_4_out_4,
       guia_0801completo_5_out_4, guia_0801meiosomador_1_out_3, guia_0805_c1_1_out_7, guia_0805_c1_1_out_8,
       guia_0805_c1_1_out_9, guia_0805_c1_1_out_10, guia_0805_c1_1_out_11, guia_0805_c1_1_out_12;

  Guia_0801completo guia_0801completo_1 (
    .out_5(out_13), .in_3(guia_0801completo_2_out_4), .in_1(guia_0805_c1_1_out_7), .in_2(in_7));  // open: out_4
  Guia_0801completo guia_0801completo_2 (
    .out_4(guia_0801completo_2_out_4), .out_5(out_14), .in_3(guia_0801completo_3_out_4),
    .in_1(guia_0805_c1_1_out_8), .in_2(in_8));
  Guia_0805_C1 guia_0805_c1_1 (
    .in_1(in_1), .in_2(in_2), .in_3(in_3), .in_4(in_4), .in_5(in_5), .in_6(in_6),
    .out_7(guia_0805_c1_1_out_7), .out_8(guia_0805_c1_1_out_8), .out_9(guia_0805_c1_1_out_9),
    .out_10(guia_0805_c1_1_out_10), .out_11(guia_0805_c1_1_out_11), .out_12(guia_0805_c1_1_out_12));
  Guia_0801completo guia_0801completo_3 (
    .out_4(guia_0801completo_3_out_4), .out_5(out_15), .in_3(guia_0801completo_4_out_4),
    .in_1(guia_0805_c1_1_out_9), .in_2(in_9));
  Guia_0801completo guia_0801completo_4 (
    .out_4(guia_0801completo_4_out_4), .out_5(out_16), .in_3(guia_0801completo_5_out_4),
    .in_1(guia_0805_c1_1_out_10), .in_2(in_10));
  Guia_0801completo guia_0801completo_5 (
    .out_4(guia_0801completo_5_out_4), .out_5(out_17), .in_3(guia_0801meiosomador_1_out_3),
    .in_1(guia_0805_c1_1_out_11), .in_2(in_11));
  Guia_0801meiosomador guia_0801meiosomador_1 (
    .out_3(guia_0801meiosomador_1_out_3), .out_4(out_18), .in_1(guia_0805_c1_1_out_12), .in_2(in_12));
endmodule
