// Logisim project Guia_R0101.circ as structural Verilog: 6 circuits, main circuit Guia_R0101a
module Guia_R0101a (
  input  a,
  input  b,
  input  c,
  input  d,
  output out_5
);

  wire and_1_out, and_2_out, and_3_out, and_4_out, and_5_out, and_6_out, and_7_out, and_8_out, not_1_out,
       not_2_out, not_3_out, not_4_out, not_5_out, not_6_out, not_7_out, not_8_out, not_9_out, not_10_out,
       not_11_out, not_12_out, not_13_out, not_14_out;

  not not_1 (not_1_out, a);
  not not_2 (not_2_out, b);
  and and_1 (and_1_out, not_1_out, not_2_out, c, d);
  not not_3 (not_3_out, a);
  not not_4 (not_4_out, b);
  and and_2 (and_2_out, not_3_out, not_4_out, c, not_5_out);
  not not_5 (not_5_out, d);
  not not_6 (not_6_out, a);
  and and_3 (and_3_out, not_6_out, b, not_7_out, not_8_out);
  not not_7 (not_7_out, c);
  not not_8 (not_8_out, d);
  not not_9 (not_9_out, a);
  and and_4 (and_4_out, not_9_out, b, not_10_out, d);
  not not_10 (not_10_out, c);
  and and_5 (and_5_out, a, b, not_11_out, d);
  not not_11 (not_11_out, c);
  and and_6 (and_6_out, a, b, c, d);
  not not_12 (not_12_out, b);
  and and_7 (and_7_out, a, not_12_out, c, d);
  not not_13 (not_13_out, b);
  and and_8 (and_8_out, a, not_13_out, c, not_14_out);
  not not_14 (not_14_out, d);
  or or_1 (out_5, and_1_out, and_2_out, and_3_out, and_4_out, and_5_out, and_6_out, and_7_out, and_8_out);

  // Notes on the sheet:
  //   a.)
endmodule

module Guia_R0101b (
  input  a,
  input  b,
  input  c,
  input  d,
  output out_5
);

  wire not_1_out, not_2_out, not_3_out, not_4_out, not_5_out, not_6_out, not_7_out, not_8_out, not_9_out,
       not_10_out, not_11_out, not_12_out, not_13_out, not_14_out, or_1_out, or_2_out, or_3_out, or_4_out,
       or_5_out, or_6_out, or_7_out, or_8_out;

  or or_1 (or_1_out, a, b, c, d);
  or or_2 (or_2_out, a, b, c, not_1_out);
  not not_1 (not_1_out, d);
  not not_2 (not_2_out, b);
  or or_3 (or_3_out, a, not_2_out, not_3_out, not_4_out);
  not not_3 (not_3_out, c);
  not not_4 (not_4_out, d);
  not not_5 (not_5_out, b);
  or or_4 (or_4_out, a, not_5_out, not_6_out, d);
  not not_6 (not_6_out, c);
  not not_7 (not_7_out, a);
  not not_8 (not_8_out, b);
  or or_5 (or_5_out, not_7_out, not_8_out, c, d);
  not not_9 (not_9_out, a);
  not not_10 (not_10_out, b);
  or or_6 (or_6_out, not_9_out, not_10_out, not_11_out, d);
  not not_11 (not_11_out, c);
  not not_12 (not_12_out, a);
  or or_7 (or_7_out, not_12_out, b, c, d);
  not not_13 (not_13_out, a);
  or or_8 (or_8_out, not_13_out, b, c, not_14_out);
  not not_14 (not_14_out, d);
  and and_1 (out_5, or_1_out, or_2_out, or_3_out, or_4_out, or_5_out, or_6_out, or_7_out, or_8_out);

  // Notes on the sheet:
  //   b.)
endmodule

module Guia_R0101c (
  input  a,
  input  b,
  input  c,
  input  d,
  output out_5
);

  wire and_1_out, and_2_out, and_3_out, not_1_out, not_2_out, not_3_out;

  not not_1 (not_1_out, a);
  not not_2 (not_2_out, c);
  not not_3 (not_3_out, b);
  and and_1 (and_1_out, not_1_out, b, not_2_out);
  and and_2 (and_2_out, a, b, d);
  and and_3 (and_3_out, not_3_out, c);
  or or_1 (out_5, and_1_out, and_2_out, and_3_out);

  // Notes on the sheet:
  //   c.)
endmodule

module Guia_R0101d (
  input  a,
  input  b,
  input  c,
  input  d,
  output out_5
);

  wire not_1_out, not_2_out, not_3_out, not_4_out, or_1_out, or_2_out, or_3_out;

  not not_1 (not_1_out, b);
  not not_2 (not_2_out, c);
  not not_3 (not_3_out, a);
  not not_4 (not_4_out, b);
  or or_1 (or_1_out, b, c);
  and and_1 (out_5, or_1_out, or_2_out, or_3_out);
  or or_2 (or_2_out, a, not_1_out, not_2_out);
  or or_3 (or_3_out, not_3_out, not_4_out, d);

  // Notes on the sheet:
  //   d.)
endmodule

module Guia_R0101e (
  input  a,
  input  b,
  input  c,
  input  d,
  output out_5
);

  wire nand_1_out, nand_2_out, nand_3_out, not_1_out, not_2_out, not_3_out;

  not not_1 (not_1_out, a);
  not not_2 (not_2_out, c);
  not not_3 (not_3_out, b);
  nand nand_1 (nand_1_out, not_1_out, b, not_2_out);
  nand nand_2 (nand_2_out, a, b, d);
  nand nand_3 (nand_3_out, not_3_out, c);
  nand nand_4 (out_5, nand_1_out, nand_2_out, nand_3_out);

  // Notes on the sheet:
  //   e.)
endmodule

module Guia_R0101f (
  input  a,
  input  b,
  input  c,
  input  d,
  output out_5
);

  wire nor_1_out, nor_2_out, nor_3_out, not_1_out, not_2_out, not_3_out, not_4_out;

  not not_1 (not_1_out, b);
  not not_2 (not_2_out, c);
  not not_3 (not_3_out, a);
  not not_4 (not_4_out, b);
  nor nor_1 (nor_1_out, b, c);
  nor nor_2 (nor_2_out, a, not_1_out, not_2_out);
  nor nor_3 (nor_3_out, not_3_out, not_4_out, d);
  nor nor_4 (out_5, nor_1_out, nor_2_out, nor_3_out);

  // Notes on the sheet:
  //   f.)
endmodule
