// Logisim project Guia_R0102.circ as structural Verilog: 1 circuit, main circuit Guia_R0102
module Guia_R0102 (
  input  a,
  input  b,
  input  c,
  output out_4
);

  wire and_1_out, and_2_out, not_1_out, not_2_out;

  not not_1 (not_1_out, c);
  not not_2 (not_2_out, b);
  and and_1 (and_1_out, not_1_out, a);
  and and_2 (and_2_out, not_2_out, c, a);
  or or_1 (out_4, and_1_out, and_2_out);
endmodule
