// Logisim project Guia_R0103.circ as structural Verilog: 2 circuits, main circuit Guia_R0103a
module Guia_R0103a (
  input  a,
  input  b,
  output out_3
);

  wire nand_1_out, nand_2_out, nor_1_out, nor_2_out;

  nor nor_1 (nor_1_out, a, a);
  nor nor_2 (nor_2_out, a, a);
  nand nand_1 (nand_1_out, nor_1_out, b);
  nand nand_2 (nand_2_out, nor_2_out, b);
  nand nand_3 (out_3, nand_1_out, nand_2_out);

  // Notes on the sheet:
  //   a.)
endmodule

module Guia_R0103b (
  input  a,
  input  b,
  input  c,
  output out_4
);

  wire multiplexer_1_out, multiplexer_2_out, not_1_out, not_2_out, not_3_out;

  Multiplexer #(.enable("false")) multiplexer_1 (.in0(b), .in1(not_1_out), .out(multiplexer_1_out), .sel(c));
  not not_1 (not_1_out, b);
  not not_2 (not_2_out, b);
  Multiplexer #(.enable("false")) multiplexer_2 (.in0(not_2_out), .in1(b), .out(multiplexer_2_out), .sel(not_3_out));
  not not_3 (not_3_out, c);
  Multiplexer #(.enable("false")) multiplexer_3 (
    .in0(multiplexer_1_out), .in1(multiplexer_2_out), .out(out_4), .sel(a));

  // Notes on the sheet:
  //   b.)
endmodule
