// Logisim project Decodificador.circ as structural Verilog
module Decodificador (
  input  e3,
  input  e2,
  input  e1,
  input  e0,
  output a,
  output b,
  output c,
  output d,
  output e,
  output f,
  output g
);

  wire and_1_out, and_2_out, and_3_out, and_4_out, and_7_out, not_1_out, not_2_out, not_3_out, not_4_out,
       not_5_out, not_6_out, not_7_out, not_8_out, not_9_out, not_10_out, not_11_out, not_12_out, not_13_out,
       not_14_out;

  not not_1 (not_1_out, e2);
  and and_1 (and_1_out, not_1_out, not_2_out);
  not not_2 (not_2_out, e0);
  not not_3 (not_3_out, e2);
  or or_1 (b, not_3_out, not_4_out);
  not not_4 (not_4_out, e0);
  not not_5 (not_5_out, e1);
  and and_2 (and_2_out, not_5_out, not_6_out);
  not not_6 (not_6_out, e0);
  not not_7 (not_7_out, e2);
  and and_3 (and_3_out, not_7_out, e0);
  not not_8 (not_8_out, e2);
  and and_4 (and_4_out, not_8_out, not_9_out);
  not not_9 (not_9_out, e0);
  not not_10 (not_10_out, e2);
  and and_5 (e, not_10_out, not_11_out);
  not not_11 (not_11_out, e0);
  not not_12 (not_12_out, e1);
  and and_6 (f, not_12_out, not_13_out);
  not not_13 (not_13_out, e0);
  and and_7 (and_7_out, e2, not_14_out);
  not not_14 (not_14_out, e0);
  or or_2 (a, and_1_out, e1);
  or or_3 (c, and_2_out, and_3_out);
  or or_4 (d, and_4_out, e1);
  or or_5 (g, e1, and_7_out);
endmodule
