// Logisim project SOMADOR.circ as structural Verilog: 3 circuits, main circuit Meia-soma
module Meia_soma (
  input  x0,
  input  y0,
  output s0,
  output carry_out
);

  xor xor_1 (s0, y0, x0);
  and and_1 (carry_out, y0, x0);
endmodule

module Soma_Completa (
  input  x,
  input  y,
  input  carry_in,
  output s0,
  output carry_out
);

  wire meia_soma_1_carry_out, meia_soma_1_s0, meia_soma_2_carry_out;

  Meia_soma meia_soma_1 (.x0(x), .y0(y), .s0(meia_soma_1_s0), .carry_out(meia_soma_1_carry_out));
  Meia_soma meia_soma_2 (.x0(meia_soma_1_s0), .y0(carry_in), .s0(s0), .carry_out(meia_soma_2_carry_out));
  or or_1 (carry_out, meia_soma_2_carry_out, meia_soma_1_carry_out);
endmodule

module soma_4_bits (
  input  in_1,
  input  in_2,
  input  in_3,
  input  in_4,
  input  in_5,
  input  in_6,
  input  in_7,
  input  in_8,
  output s0,
  output s1,
  output s2,
  output s3,
  output Carry_out
);

  wire soma_completa_1_carry_out, soma_completa_2_carry_out, soma_completa_3_carry_out;

  Soma_Completa soma_completa_1 (.x(in_1), .y(in_5), .carry_in(1'b0), .s0(s0), .carry_out(soma_completa_1_carry_out));
  Soma_Completa soma_completa_2 (
    .x(in_2), .y(in_6), .carry_in(soma_completa_1_carry_out), .s0(s1), .carry_out(soma_completa_2_carry_out));
  Soma_Completa soma_completa_3 (
    .x(in_3), .y(in_7), .carry_in(soma_completa_2_carry_out), .s0(s2), .carry_out(soma_completa_3_carry_out));
  Soma_Completa soma_completa_4 (
    .x(in_4), .y(in_8), .carry_in(soma_completa_3_carry_out), .s0(s3), .carry_out(Carry_out));
endmodule
