// Logisim project Somador4bits.circ as structural Verilog: 6 circuits, main circuit main
module main (
  input  A0,
  input  A1,
  input  A2,
  input  A3,
  input  Ci,
  input  B0,
  input  B1,
  input  B2,
  input  B3,
  output Carry_out,
  output S0,
  output S1,
  output S2,
  output S3,
  output Overflow
);

  wire decodificador_hexa_1_a, decodificador_hexa_1_b, decodificador_hexa_1_c, decodificador_hexa_1_d,
       decodificador_hexa_1_e, decodificador_hexa_1_f, decodificador_hexa_1_g, decodificador_hexa_2_a,
       decodificador_hexa_2_b, decodificador_hexa_2_c, decodificador_hexa_2_d, decodificador_hexa_2_e,
       decodificador_hexa_2_f, decodificador_hexa_2_g, decodificador_hexa_3_a, decodificador_hexa_3_b,
       decodificador_hexa_3_c, decodificador_hexa_3_d, decodificador_hexa_3_e, decodificador_hexa_3_f,
       decodificador_hexa_3_g;

  decodificador_hexa decodificador_hexa_1 (
    .e1(A0), .e2(A1), .e3(A2), .e4(A3), .a(decodificador_hexa_1_a), .b(decodificador_hexa_1_b),
    .c(decodificador_hexa_1_c), .d(decodificador_hexa_1_d), .e(decodificador_hexa_1_e),
    .f(decodificador_hexa_1_f), .g(decodificador_hexa_1_g));
  Soma_4_bits soma_4_bits_1 (
    .x3(A0), .x2(A1), .x1(A2), .x0(A3), .y3(B0), .y2(B1), .y1(B2), .y0(B3), .in_2(Ci), .Overflow(Overflow),
    .s3(S0), .s2(S1), .s1(S2), .s0(S3), .Carry_out(Carry_out));
  decodificador_hexa decodificador_hexa_2 (
    .e1(B0), .e2(B1), .e3(B2), .e4(B3), .a(decodificador_hexa_2_a), .b(decodificador_hexa_2_b),
    .c(decodificador_hexa_2_c), .d(decodificador_hexa_2_d), .e(decodificador_hexa_2_e),
    .f(decodificador_hexa_2_f), .g(decodificador_hexa_2_g));
  _7_Segment_Display u_7_segment_display_1 (
    .g(decodificador_hexa_1_g), .f(decodificador_hexa_1_f), .a(decodificador_hexa_1_a),
    .b(decodificador_hexa_1_b), .e(decodificador_hexa_1_e), .d(decodificador_hexa_1_d),
    .c(decodificador_hexa_1_c));  // open: dp
  _7_Segment_Display u_7_segment_display_2 (
    .g(decodificador_hexa_2_g), .f(decodificador_hexa_2_f), .a(decodificador_hexa_2_a),
    .b(decodificador_hexa_2_b), .e(decodificador_hexa_2_e), .d(decodificador_hexa_2_d),
    .c(decodificador_hexa_2_c));  // open: dp
  decodificador_hexa decodificador_hexa_3 (
    .e1(S0), .e2(S1), .e3(S2), .e4(S3), .a(decodificador_hexa_3_a), .b(decodificador_hexa_3_b),
    .c(decodificador_hexa_3_c), .d(decodificador_hexa_3_d), .e(decodificador_hexa_3_e),
    .f(decodificador_hexa_3_f), .g(decodificador_hexa_3_g));
  _7_Segment_Display u_7_segment_display_3 (
    .g(decodificador_hexa_3_g), .f(decodificador_hexa_3_f), .a(decodificador_hexa_3_a),
    .b(decodificador_hexa_3_b), .e(decodificador_hexa_3_e), .d(decodificador_hexa_3_d),
    .c(decodificador_hexa_3_c));  // open: dp
endmodule

module decodificador_hexa (
  input  e1,
  input  e2,
  input  e3,
  input  e4,
  output a,
  output b,
  output c,
  output d,
  output e,
  output f,
  output g
);

  wire and_1_out, and_2_out, and_3_out, and_4_out, and_5_out, and_6_out, and_7_out, and_8_out, and_9_out,
       and_10_out, and_11_out, and_12_out, and_13_out, and_14_out, and_15_out, and_16_out, and_17_out,
       and_18_out, and_19_out, and_20_out, and_21_out, and_22_out, and_23_out, and_24_out, and_25_out,
       and_26_out, and_27_out, and_28_out, and_29_out, and_30_out, and_31_out, and_32_out, and_33_out,
       and_34_out, and_35_out, not_1_out, not_2_out, not_3_out, not_4_out, not_5_out, not_6_out, not_7_out,
       not_8_out, not_9_out, not_10_out, not_11_out, not_12_out, not_13_out, not_14_out, not_15_out,
       not_16_out, not_17_out, not_18_out, not_19_out, not_20_out, not_21_out, not_22_out, not_23_out,
       not_24_out, not_25_out, not_26_out, not_27_out, not_28_out, not_29_out, not_30_out, not_31_out,
       not_32_out, not_33_out, not_34_out, not_35_out, not_36_out, not_37_out, not_38_out, not_39_out,
       not_40_out, not_41_out, not_42_out, not_43_out;

  not not_1 (not_1_out, e2);
  and and_1 (and_1_out, not_1_out, not_2_out);
  not not_2 (not_2_out, e4);
  not not_3 (not_3_out, e1);
  and and_2 (and_2_out, not_3_out, e3);
  not not_4 (not_4_out, e1);
  and and_3 (and_3_out, not_4_out, e2, e4);
  and and_4 (and_4_out, e2, e3);
  not not_5 (not_5_out, e2);
  and and_5 (and_5_out, e1, not_5_out, not_6_out);
  not not_6 (not_6_out, e3);
  and and_6 (and_6_out, e1, not_7_out);
  not not_7 (not_7_out, e4);
  not not_8 (not_8_out, e1);
  and and_7 (and_7_out, not_8_out, not_9_out);
  not not_9 (not_9_out, e2);
  not not_10 (not_10_out, e1);
  not not_11 (not_11_out, e3);
  and and_8 (and_8_out, not_10_out, not_11_out, not_12_out);
  not not_12 (not_12_out, e4);
  not not_13 (not_13_out, e2);
  and and_9 (and_9_out, not_13_out, not_14_out);
  not not_14 (not_14_out, e4);
  not not_15 (not_15_out, e1);
  and and_10 (and_10_out, not_15_out, e3, e4);
  not not_16 (not_16_out, e3);
  and and_11 (and_11_out, e1, not_16_out, e4);
  not not_17 (not_17_out, e1);
  and and_12 (and_12_out, not_17_out, not_18_out);
  not not_18 (not_18_out, e3);
  not not_19 (not_19_out, e1);
  and and_13 (and_13_out, not_19_out, e4);
  not not_20 (not_20_out, e3);
  and and_14 (and_14_out, not_20_out, e4);
  not not_21 (not_21_out, e1);
  and and_15 (and_15_out, not_21_out, e2);
  and and_16 (and_16_out, e1, not_22_out);
  not not_22 (not_22_out, e2);
  not not_23 (not_23_out, e1);
  and and_17 (and_17_out, not_23_out, not_24_out, not_25_out);
  not not_24 (not_24_out, e2);
  not not_25 (not_25_out, e4);
  not not_26 (not_26_out, e2);
  and and_18 (and_18_out, not_26_out, e3, e4);
  not not_27 (not_27_out, e3);
  and and_19 (and_19_out, e2, not_27_out, e4);
  and and_20 (and_20_out, e2, e3, not_28_out);
  not not_28 (not_28_out, e4);
  and and_21 (and_21_out, e1, not_29_out);
  not not_29 (not_29_out, e3);
  not not_30 (not_30_out, e2);
  and and_22 (and_22_out, not_30_out, not_31_out);
  not not_31 (not_31_out, e4);
  and and_23 (and_23_out, e3, not_32_out);
  not not_32 (not_32_out, e4);
  and and_24 (and_24_out, e1, e3);
  and and_25 (and_25_out, e1, e2);
  not not_33 (not_33_out, e3);
  and and_26 (and_26_out, not_33_out, not_34_out);
  not not_34 (not_34_out, e4);
  not not_35 (not_35_out, e1);
  and and_27 (and_27_out, not_35_out, e2, not_36_out);
  not not_36 (not_36_out, e3);
  and and_28 (and_28_out, e2, not_37_out);
  not not_37 (not_37_out, e4);
  and and_29 (and_29_out, e1, not_38_out);
  not not_38 (not_38_out, e2);
  and and_30 (and_30_out, e1, e3);
  not not_39 (not_39_out, e2);
  and and_31 (and_31_out, not_39_out, e3);
  and and_32 (and_32_out, e3, not_40_out);
  not not_40 (not_40_out, e4);
  not not_41 (not_41_out, e1);
  and and_33 (and_33_out, not_41_out, e2, not_42_out);
  not not_42 (not_42_out, e3);
  and and_34 (and_34_out, e1, not_43_out);
  not not_43 (not_43_out, e2);
  and and_35 (and_35_out, e1, e4);
  or or_1 (b, and_7_out, and_8_out, and_9_out, and_10_out, and_11_out);
  or or_2 (c, and_12_out, and_13_out, and_14_out, and_15_out, and_16_out);
  or or_3 (d, and_17_out, and_18_out, and_19_out, and_20_out, and_21_out);
  or or_4 (e, and_22_out, and_23_out, and_24_out, and_25_out);
  or or_5 (f, and_26_out, and_27_out, and_28_out, and_29_out, and_30_out);
  or or_6 (g, and_31_out, and_32_out, and_33_out, and_34_out, and_35_out);
  or or_7 (a, and_1_out, and_2_out, and_3_out, and_4_out, and_5_out, and_6_out);
endmodule

module Somador_4_bits (
  input  A0,
  input  A1,
  input  A2,
  input  A3,
  input  B0,
  input  B1,
  input  B2,
  input  B3,
  output S0,
  output S1,
  output S2,
  output S3,
  output Overflow
);

  wire and_1_out, and_2_out, and_3_out, and_4_out, and_5_out, and_6_out, and_7_out, and_8_out, and_9_out,
       and_10_out, and_11_out, and_12_out, and_13_out, and_14_out, and_15_out, and_16_out, and_17_out,
       and_18_out, and_19_out, and_20_out, and_21_out, and_22_out, and_23_out, and_24_out, and_25_out,
       and_26_out, and_27_out, and_28_out, and_29_out, and_30_out, and_31_out, and_32_out, and_33_out,
       and_34_out, and_35_out, and_36_out, and_37_out, and_38_out, and_39_out, and_40_out, and_41_out,
       and_42_out, and_43_out, and_44_out, and_45_out, and_46_out, and_47_out, and_48_out, and_49_out,
       and_50_out, and_51_out, and_52_out, and_53_out, and_54_out, and_55_out, and_56_out, and_57_out,
       and_58_out, and_59_out, and_60_out, and_61_out, and_62_out, and_63_out, and_64_out, and_65_out,
       and_66_out, and_67_out, and_68_out, and_69_out, and_70_out, and_71_out, and_72_out, and_73_out,
       and_74_out, and_75_out, not_1_out, not_2_out, not_3_out, not_4_out, not_5_out, not_6_out, not_7_out,
       not_8_out, not_9_out, not_10_out, not_11_out, not_12_out, not_13_out, not_14_out, not_15_out,
       not_16_out, not_17_out, not_18_out, not_19_out, not_20_out, not_21_out, not_22_out, not_23_out,
       not_24_out, not_25_out, not_26_out, not_27_out, not_28_out, not_29_out, not_30_out, not_31_out,
       not_32_out, not_33_out, not_34_out, not_35_out, not_36_out, not_37_out, not_38_out, not_39_out,
       not_40_out, not_41_out, not_42_out, not_43_out, not_44_out, not_45_out, not_46_out, not_47_out,
       not_48_out, not_49_out, not_50_out, not_51_out, not_52_out, not_53_out, not_54_out, not_55_out,
       not_56_out, not_57_out, not_58_out, not_59_out, not_60_out, not_61_out, not_62_out, not_63_out,
       not_64_out, not_65_out, not_66_out, not_67_out, not_68_out, not_69_out, not_70_out, not_71_out,
       not_72_out, not_73_out, not_74_out, not_75_out, not_76_out, not_77_out, not_78_out, not_79_out,
       not_80_out, not_81_out, not_82_out, not_83_out, not_84_out, not_85_out, not_86_out, not_87_out,
       not_88_out, not_89_out, not_90_out, not_91_out, not_92_out, not_93_out, not_94_out, not_95_out,
       not_96_out, not_97_out, not_98_out, not_99_out, not_100_out, not_101_out, not_102_out, not_103_out,
       not_104_out, not_105_out, not_106_out, not_107_out, not_108_out, not_109_out, not_110_out,
       not_111_out, not_112_out, not_113_out, not_114_out, not_115_out, not_116_out, not_117_out,
       not_118_out, not_119_out, not_120_out, not_121_out, not_122_out, not_123_out, not_124_out,
       not_125_out, not_126_out, not_127_out, not_128_out, not_129_out, not_130_out, not_131_out,
       not_132_out, not_133_out, not_134_out, not_135_out, not_136_out, not_137_out, not_138_out,
       not_139_out, not_140_out, not_141_out, not_142_out, not_143_out, not_144_out, not_145_out,
       not_146_out, not_147_out, not_148_out, or_5_out, or_7_out;

  not not_1 (not_1_out, A0);
  not not_2 (not_2_out, A1);
  not not_3 (not_3_out, A2);
  not not_4 (not_4_out, A3);
  not not_5 (not_5_out, A0);
  not not_6 (not_6_out, A1);
  not not_7 (not_7_out, A2);
  not not_8 (not_8_out, B2);
  not not_9 (not_9_out, A0);
  not not_10 (not_10_out, A1);
  not not_11 (not_11_out, A2);
  not not_12 (not_12_out, B3);
  not not_13 (not_13_out, A0);
  not not_14 (not_14_out, A1);
  not not_15 (not_15_out, A3);
  not not_16 (not_16_out, B2);
  not not_17 (not_17_out, A0);
  not not_18 (not_18_out, A1);
  not not_19 (not_19_out, B1);
  not not_20 (not_20_out, A0);
  not not_21 (not_21_out, A1);
  not not_22 (not_22_out, B2);
  not not_23 (not_23_out, B3);
  not not_24 (not_24_out, A0);
  not not_25 (not_25_out, A2);
  not not_26 (not_26_out, A3);
  not not_27 (not_27_out, B1);
  not not_28 (not_28_out, A0);
  not not_29 (not_29_out, A2);
  not not_30 (not_30_out, B1);
  not not_31 (not_31_out, B2);
  not not_32 (not_32_out, A0);
  not not_33 (not_33_out, A2);
  not not_34 (not_34_out, B1);
  not not_35 (not_35_out, B3);
  not not_36 (not_36_out, A0);
  not not_37 (not_37_out, A3);
  not not_38 (not_38_out, B1);
  not not_39 (not_39_out, B2);
  not not_40 (not_40_out, A0);
  not not_41 (not_41_out, B1);
  not not_42 (not_42_out, B2);
  not not_43 (not_43_out, B3);
  not not_44 (not_44_out, A0);
  not not_45 (not_45_out, B0);
  not not_46 (not_46_out, A0);
  not not_47 (not_47_out, B0);
  not not_48 (not_48_out, A0);
  not not_49 (not_49_out, B0);
  not not_50 (not_50_out, A0);
  not not_51 (not_51_out, B0);
  not not_52 (not_52_out, A0);
  not not_53 (not_53_out, B0);
  not not_54 (not_54_out, A0);
  not not_55 (not_55_out, B0);
  not not_56 (not_56_out, A0);
  not not_57 (not_57_out, B0);
  not not_58 (not_58_out, A1);
  not not_59 (not_59_out, A2);
  not not_60 (not_60_out, A3);
  not not_61 (not_61_out, B0);
  not not_62 (not_62_out, A1);
  not not_63 (not_63_out, A2);
  not not_64 (not_64_out, B0);
  not not_65 (not_65_out, B2);
  not not_66 (not_66_out, A1);
  not not_67 (not_67_out, A2);
  not not_68 (not_68_out, B0);
  not not_69 (not_69_out, B3);
  not not_70 (not_70_out, A1);
  not not_71 (not_71_out, A3);
  not not_72 (not_72_out, B0);
  not not_73 (not_73_out, B2);
  not not_74 (not_74_out, A1);
  not not_75 (not_75_out, B0);
  not not_76 (not_76_out, B1);
  not not_77 (not_77_out, A1);
  not not_78 (not_78_out, B0);
  not not_79 (not_79_out, B2);
  not not_80 (not_80_out, B3);
  not not_81 (not_81_out, A2);
  not not_82 (not_82_out, A3);
  not not_83 (not_83_out, B0);
  not not_84 (not_84_out, B1);
  not not_85 (not_85_out, A2);
  not not_86 (not_86_out, B0);
  not not_87 (not_87_out, B1);
  not not_88 (not_88_out, B2);
  not not_89 (not_89_out, A2);
  not not_90 (not_90_out, B0);
  not not_91 (not_91_out, B1);
  not not_92 (not_92_out, B3);
  not not_93 (not_93_out, A3);
  not not_94 (not_94_out, B0);
  not not_95 (not_95_out, B1);
  not not_96 (not_96_out, B2);
  not not_97 (not_97_out, B0);
  not not_98 (not_98_out, B1);
  not not_99 (not_99_out, B2);
  not not_100 (not_100_out, B3);
  not not_101 (not_101_out, A1);
  not not_102 (not_102_out, A2);
  not not_103 (not_103_out, A3);
  not not_104 (not_104_out, A1);
  not not_105 (not_105_out, A2);
  not not_106 (not_106_out, B2);
  not not_107 (not_107_out, A1);
  not not_108 (not_108_out, A2);
  not not_109 (not_109_out, B3);
  not not_110 (not_110_out, A1);
  not not_111 (not_111_out, A3);
  not not_112 (not_112_out, B2);
  not not_113 (not_113_out, A1);
  not not_114 (not_114_out, B2);
  not not_115 (not_115_out, B3);
  not not_116 (not_116_out, A1);
  not not_117 (not_117_out, B1);
  not not_118 (not_118_out, A1);
  not not_119 (not_119_out, B1);
  not not_120 (not_120_out, A1);
  not not_121 (not_121_out, B1);
  not not_122 (not_122_out, A2);
  not not_123 (not_123_out, A3);
  not not_124 (not_124_out, B1);
  not not_125 (not_125_out, A2);
  not not_126 (not_126_out, B1);
  not not_127 (not_127_out, B2);
  not not_128 (not_128_out, A2);
  not not_129 (not_129_out, B1);
  not not_130 (not_130_out, B3);
  not not_131 (not_131_out, A3);
  not not_132 (not_132_out, B1);
  not not_133 (not_133_out, B2);
  not not_134 (not_134_out, B1);
  not not_135 (not_135_out, B2);
  not not_136 (not_136_out, B3);
  not not_137 (not_137_out, A2);
  not not_138 (not_138_out, A3);
  not not_139 (not_139_out, A2);
  not not_140 (not_140_out, B3);
  not not_141 (not_141_out, A2);
  not not_142 (not_142_out, B2);
  not not_143 (not_143_out, A3);
  not not_144 (not_144_out, B2);
  not not_145 (not_145_out, B2);
  not not_146 (not_146_out, B3);
  not not_147 (not_147_out, A3);
  and and_1 (and_1_out, not_147_out, B3);
  and and_2 (and_2_out, A3, not_148_out);
  not not_148 (not_148_out, B3);
  and and_3 (and_3_out, A3, B0, B1, B2, B3);
  and and_4 (and_4_out, A2, B0, B1, B2);
  and and_5 (and_5_out, A2, A3, B0, B1, B3);
  and and_6 (and_6_out, A1, B0, B1);
  and and_7 (and_7_out, A1, A3, B0, B2, B3);
  and and_8 (and_8_out, A1, A2, B0, B2);
  and and_9 (and_9_out, A1, A2, A3, B0, B3);
  and and_10 (and_10_out, A0, B0);
  and and_11 (and_11_out, A0, A3, B1, B2, B3);
  and and_12 (and_12_out, A0, A2, B1, B2);
  and and_13 (and_13_out, A0, A2, A3, B1, B3);
  and and_14 (and_14_out, A0, A1, B1);
  and and_15 (and_15_out, A0, A1, A3, B2, B3);
  and and_16 (and_16_out, A0, A1, A2, B2);
  and and_17 (and_17_out, A0, A1, A2, A3, B3);
  and and_18 (and_18_out, not_1_out, not_2_out, not_3_out, not_4_out, B0);
  and and_19 (and_19_out, not_5_out, not_6_out, not_7_out, B0, not_8_out);
  and and_20 (and_20_out, not_9_out, not_10_out, not_11_out, B0, not_12_out);
  and and_21 (and_21_out, not_13_out, not_14_out, not_15_out, B0, not_16_out);
  and and_22 (and_22_out, not_17_out, not_18_out, B0, not_19_out);
  and and_23 (and_23_out, not_20_out, not_21_out, B0, not_22_out, not_23_out);
  and and_24 (and_24_out, not_24_out, not_25_out, not_26_out, B0, not_27_out);
  and and_25 (and_25_out, not_28_out, not_29_out, B0, not_30_out, not_31_out);
  and and_26 (and_26_out, not_32_out, not_33_out, B0, not_34_out, not_35_out);
  and and_27 (and_27_out, not_36_out, not_37_out, B0, not_38_out, not_39_out);
  and and_28 (and_28_out, not_40_out, B0, not_41_out, not_42_out, not_43_out);
  and and_29 (and_29_out, not_44_out, A3, not_45_out, B1, B2, B3);
  and and_30 (and_30_out, not_46_out, A2, not_47_out, B1, B2);
  and and_31 (and_31_out, not_48_out, A2, A3, not_49_out, B1, B3);
  and and_32 (and_32_out, not_50_out, A1, not_51_out, B1);
  and and_33 (and_33_out, not_52_out, A1, A3, not_53_out, B2, B3);
  and and_34 (and_34_out, not_54_out, A1, A2, not_55_out, B2);
  and and_35 (and_35_out, not_56_out, A1, A2, A3, not_57_out, B3);
  and and_36 (and_36_out, A0, not_58_out, not_59_out, not_60_out, not_61_out);
  and and_37 (and_37_out, A0, not_62_out, not_63_out, not_64_out, not_65_out);
  and and_38 (and_38_out, A0, not_66_out, not_67_out, not_68_out, not_69_out);
  and and_39 (and_39_out, A0, not_70_out, not_71_out, not_72_out, not_73_out);
  and and_40 (and_40_out, A0, not_74_out, not_75_out, not_76_out);
  and and_41 (and_41_out, A0, not_77_out, not_78_out, not_79_out, not_80_out);
  and and_42 (and_42_out, A0, not_81_out, not_82_out, not_83_out, not_84_out);
  and and_43 (and_43_out, A0, not_85_out, not_86_out, not_87_out, not_88_out);
  and and_44 (and_44_out, A0, not_89_out, not_90_out, not_91_out, not_92_out);
  and and_45 (and_45_out, A0, not_93_out, not_94_out, not_95_out, not_96_out);
  and and_46 (and_46_out, A0, not_97_out, not_98_out, not_99_out, not_100_out);
  and and_47 (and_47_out, A0, A3, B0, B1, B2, B3);
  and and_48 (and_48_out, A0, A2, B0, B1, B2);
  and and_49 (and_49_out, A0, A2, A3, B0, B1, B3);
  and and_50 (and_50_out, A0, A1, B0, B1);
  and and_51 (and_51_out, A0, A1, A3, B0, B2, B3);
  and and_52 (and_52_out, A0, A1, A2, B0, B2);
  and and_53 (and_53_out, A0, A1, A2, A3, B0, B3);
  and and_54 (and_54_out, not_101_out, not_102_out, not_103_out, B1);
  and and_55 (and_55_out, not_104_out, not_105_out, B1, not_106_out);
  and and_56 (and_56_out, not_107_out, not_108_out, B1, not_109_out);
  and and_57 (and_57_out, not_110_out, not_111_out, B1, not_112_out);
  and and_58 (and_58_out, not_113_out, B1, not_114_out, not_115_out);
  and and_59 (and_59_out, not_116_out, A3, not_117_out, B2, B3);
  and and_60 (and_60_out, not_118_out, A2, not_119_out, B2);
  and and_61 (and_61_out, not_120_out, A2, A3, not_121_out, B3);
  and and_62 (and_62_out, A1, not_122_out, not_123_out, not_124_out);
  and and_63 (and_63_out, A1, not_125_out, not_126_out, not_127_out);
  and and_64 (and_64_out, A1, not_128_out, not_129_out, not_130_out);
  and and_65 (and_65_out, A1, not_131_out, not_132_out, not_133_out);
  and and_66 (and_66_out, A1, not_134_out, not_135_out, not_136_out);
  and and_67 (and_67_out, A1, A3, B1, B2, B3);
  and and_68 (and_68_out, A1, A2, B1, B2);
  and and_69 (and_69_out, A1, A2, A3, B1, B3);
  and and_70 (and_70_out, not_137_out, not_138_out, B2);
  and and_71 (and_71_out, not_139_out, B2, not_140_out);
  and and_72 (and_72_out, not_141_out, A3, not_142_out, B3);
  and and_73 (and_73_out, A2, not_143_out, not_144_out);
  and and_74 (and_74_out, A2, not_145_out, not_146_out);
  and and_75 (and_75_out, A2, A3, B2, B3);
  or or_1 (S3, and_1_out, and_2_out);
  or or_2 (Overflow, and_3_out, and_4_out, and_5_out, and_6_out, and_7_out, and_8_out, and_9_out, and_10_out, and_11_out, and_12_out, and_13_out, and_14_out, and_15_out, and_16_out, and_17_out);
  or or_3 (S1, and_54_out, and_55_out, and_56_out, and_57_out, and_58_out, and_59_out, and_60_out, and_61_out, and_62_out, and_63_out, and_64_out, and_65_out, and_66_out, and_67_out, and_68_out, and_69_out);
  or or_4 (S2, and_70_out, and_71_out, and_72_out, and_73_out, and_74_out, and_75_out);
  or or_5 (or_5_out, and_18_out, and_19_out, and_20_out, and_21_out, and_22_out, and_23_out, and_24_out, and_25_out, and_26_out, and_27_out, and_28_out, and_29_out, and_30_out, and_31_out, and_32_out, and_33_out, and_34_out, and_35_out);
  or or_6 (S0, or_5_out, or_7_out);
  or or_7 (or_7_out, and_36_out, and_37_out, and_38_out, and_39_out, and_40_out, and_41_out, and_42_out, and_43_out, and_44_out, and_45_out, and_46_out, and_47_out, and_48_out, and_49_out, and_50_out, and_51_out, and_52_out, and_53_out);
endmodule

module Meia_soma (
  input  x0,
  input  y0,
  output s0,
  output carry_out
);

  xor xor_1 (s0, y0, x0);
  and and_1 (carry_out, y0, x0);
endmodule

module Soma_Completa (
  input  x,
  input  y,
  input  carry_in,
  output s0,
  output carry_out
);

  wire meia_soma_1_carry_out, meia_soma_1_s0, meia_soma_2_carry_out;

  SOMADOR_Meia_soma meia_soma_1 (.x0(x), .y0(y), .s0(meia_soma_1_s0), .carry_out(meia_soma_1_carry_out));
  SOMADOR_Meia_soma meia_soma_2 (.x0(meia_soma_1_s0), .y0(carry_in), .s0(s0), .carry_out(meia_soma_2_carry_out));
  or or_1 (carry_out, meia_soma_2_carry_out, meia_soma_1_carry_out);
endmodule

module Soma_4_bits (
  input  x3,
  input  in_2,
  input  x2,
  input  x1,
  input  x0,
  input  y3,
  input  y2,
  input  y1,
  input  y0,
  output s3,
  output s2,
  output s1,
  output s0,
  output Carry_out,
  output Overflow
);

  wire and_1_out, and_2_out, and_3_out, nand_1_out, not_1_out, soma_completa_1_carry_out,
       soma_completa_2_carry_out, soma_completa_3_carry_out;

  and and_1 (and_1_out, x3, y3);
  not not_1 (not_1_out, s3);
  and and_2 (and_2_out, not_1_out, and_1_out);
  SOMADOR_Soma_Completa soma_completa_1 (
    .x(x0), .y(y0), .carry_in(in_2), .s0(s0), .carry_out(soma_completa_1_carry_out));
  SOMADOR_Soma_Completa soma_completa_2 (
    .x(x1), .y(y1), .carry_in(soma_completa_1_carry_out), .s0(s1), .carry_out(soma_completa_2_carry_out));
  SOMADOR_Soma_Completa soma_completa_3 (
    .x(y2), .y(x2), .carry_in(soma_completa_2_carry_out), .s0(s2), .carry_out(soma_completa_3_carry_out));
  SOMADOR_Soma_Completa soma_completa_4 (
    .x(x3), .y(y3), .carry_in(soma_completa_3_carry_out), .s0(s3), .carry_out(Carry_out));
  nand nand_1 (nand_1_out, x3, y3);
  and and_3 (and_3_out, nand_1_out, s3);
  or or_1 (Overflow, and_2_out, and_3_out);
endmodule
