// Logisim project Somador4bits_2.0.circ as structural Verilog: 5 circuits, main circuit main
module main (
  input  A3,
  input  A2,
  input  A1,
  input  A0,
  input  Ci,
  input  B3,
  input  B2,
  input  B1,
  input  B0,
  output Carry_out,
  output S3,
  output S2,
  output S1,
  output S0,
  output Overflow
);

  wire decodificador_hexa_1_a, decodificador_hexa_1_b, decodificador_hexa_1_c, decodificador_hexa_1_d,
       decodificador_hexa_1_e, decodificador_hexa_1_f, decodificador_hexa_1_g, decodificador_hexa_2_a,
       decodificador_hexa_2_b, decodificador_hexa_2_c, decodificador_hexa_2_d, decodificador_hexa_2_e,
       decodificador_hexa_2_f, decodificador_hexa_2_g, decodificador_hexa_3_a, decodificador_hexa_3_b,
       decodificador_hexa_3_c, decodificador_hexa_3_d, decodificador_hexa_3_e, decodificador_hexa_3_f,
       decodificador_hexa_3_g;

  decodificador_hexa decodificador_hexa_1 (
    .e1(A3), .e2(A2), .e3(A1), .e4(A0), .a(decodificador_hexa_1_a), .b(decodificador_hexa_1_b),
    .c(decodificador_hexa_1_c), .d(decodificador_hexa_1_d), .e(decodificador_hexa_1_e),
    .f(decodificador_hexa_1_f), .g(decodificador_hexa_1_g));
  Soma_4_bits soma_4_bits_1 (
    .x3(A3), .x2(A2), .x1(A1), .x0(A0), .y3(B3), .y2(B2), .y1(B1), .y0(B0), .in_2(Ci), .Overflow(Overflow),
    .s3(S3), .s2(S2), .s1(S1), .s0(S0), .Carry_out(Carry_out));
  decodificador_hexa decodificador_hexa_2 (
    .e1(B3), .e2(B2), .e3(B1), .e4(B0), .a(decodificador_hexa_2_a), .b(decodificador_hexa_2_b),
    .c(decodificador_hexa_2_c), .d(decodificador_hexa_2_d), .e(decodificador_hexa_2_e),
    .f(decodificador_hexa_2_f), .g(decodificador_hexa_2_g));
  _7_Segment_Display u_7_segment_display_1 (
    .g(decodificador_hexa_1_g), .f(decodificador_hexa_1_f), .a(decodificador_hexa_1_a),
    .b(decodificador_hexa_1_b), .e(decodificador_hexa_1_e), .d(decodificador_hexa_1_d),
    .c(decodificador_hexa_1_c));  // open: dp
  _7_Segment_Display u_7_segment_display_2 (
    .g(decodificador_hexa_2_g), .f(decodificador_hexa_2_f), .a(decodificador_hexa_2_a),
    .b(decodificador_hexa_2_b), .e(decodificador_hexa_2_e), .d(decodificador_hexa_2_d),
    .c(decodificador_hexa_2_c));  // open: dp
  decodificador_hexa decodificador_hexa_3 (
    .e1(S3), .e2(S2), .e3(S1), .e4(S0), .a(decodificador_hexa_3_a), .b(decodificador_hexa_3_b),
    .c(decodificador_hexa_3_c), .d(decodificador_hexa_3_d), .e(decodificador_hexa_3_e),
    .f(decodificador_hexa_3_f), .g(decodificador_hexa_3_g));
  _7_Segment_Display u_7_segment_display_3 (
    .g(decodificador_hexa_3_g), .f(decodificador_hexa_3_f), .a(decodificador_hexa_3_a),
    .b(decodificador_hexa_3_b), .e(decodificador_hexa_3_e), .d(decodificador_hexa_3_d),
    .c(decodificador_hexa_3_c));  // open: dp
endmodule

module decodificador_hexa (
  input  e1,
  input  e2,
  input  e3,
  input  e4,
  output a,
  output b,
  output c,
  output d,
  output e,
  output f,
  output g
);

  wire and_1_out, and_2_out, and_3_out, and_4_out, and_5_out, and_6_out, and_7_out, and_8_out, and_9_out,
       and_10_out, and_11_out, and_12_out, and_13_out, and_14_out, and_15_out, and_16_out, and_17_out,
       and_18_out, and_19_out, and_20_out, and_21_out, and_22_out, and_23_out, and_24_out, and_25_out,
       and_26_out, and_27_out, and_28_out, and_29_out, and_30_out, and_31_out, and_32_out, and_33_out,
       and_34_out, and_35_out, not_1_out, not_2_out, not_3_out, not_4_out, not_5_out, not_6_out, not_7_out,
       not_8_out, not_9_out, not_10_out, not_11_out, not_12_out, not_13_out, not_14_out, not_15_out,
       not_16_out, not_17_out, not_18_out, not_19_out, not_20_out, not_21_out, not_22_out, not_23_out,
       not_24_out, not_25_out, not_26_out, not_27_out, not_28_out, not_29_out, not_30_out, not_31_out,
       not_32_out, not_33_out, not_34_out, not_35_out, not_36_out, not_37_out, not_38_out, not_39_out,
       not_40_out, not_41_out, not_42_out, not_43_out;

  not not_1 (not_1_out, e2);
  and and_1 (and_1_out, not_1_out, not_2_out);
  not not_2 (not_2_out, e4);
  not not_3 (not_3_out, e1);
  and and_2 (and_2_out, not_3_out, e3);
  not not_4 (not_4_out, e1);
  and and_3 (and_3_out, not_4_out, e2, e4);
  and and_4 (and_4_out, e2, e3);
  and and_5 (and_5_out, e1, not_5_out, not_6_out);
  not not_5 (not_5_out, e2);
  not not_6 (not_6_out, e3);
  and and_6 (and_6_out, e1, not_7_out);
  not not_7 (not_7_out, e4);
  not not_8 (not_8_out, e1);
  and and_7 (and_7_out, not_8_out, not_9_out);
  not not_9 (not_9_out, e2);
  not not_10 (not_10_out, e1);
  and and_8 (and_8_out, not_10_out, not_11_out, not_12_out);
  not not_11 (not_11_out, e3);
  not not_12 (not_12_out, e4);
  not not_13 (not_13_out, e2);
  and and_9 (and_9_out, not_13_out, not_14_out);
  not not_14 (not_14_out, e4);
  not not_15 (not_15_out, e1);
  and and_10 (and_10_out, not_15_out, e3, e4);
  not not_16 (not_16_out, e3);
  and and_11 (and_11_out, e1, not_16_out, e4);
  not not_17 (not_17_out, e1);
  and and_12 (and_12_out, not_17_out, not_18_out);
  not not_18 (not_18_out, e3);
  not not_19 (not_19_out, e1);
  and and_13 (and_13_out, not_19_out, e4);
  not not_20 (not_20_out, e3);
  and and_14 (and_14_out, not_20_out, e4);
  not not_21 (not_21_out, e1);
  and and_15 (and_15_out, not_21_out, e2);
  and and_16 (and_16_out, e1, not_22_out);
  not not_22 (not_22_out, e2);
  not not_23 (not_23_out, e1);
  and and_17 (and_17_out, not_23_out, not_24_out, not_25_out);
  not not_24 (not_24_out, e2);
  not not_25 (not_25_out, e4);
  not not_26 (not_26_out, e2);
  and and_18 (and_18_out, not_26_out, e3, e4);
  and and_19 (and_19_out, e2, not_27_out, e4);
  not not_27 (not_27_out, e3);
  and and_20 (and_20_out, e2, e3, not_28_out);
  not not_28 (not_28_out, e4);
  and and_21 (and_21_out, e1, not_29_out);
  not not_29 (not_29_out, e3);
  not not_30 (not_30_out, e2);
  and and_22 (and_22_out, not_30_out, not_31_out);
  not not_31 (not_31_out, e4);
  and and_23 (and_23_out, e3, not_32_out);
  not not_32 (not_32_out, e4);
  and and_24 (and_24_out, e1, e3);
  and and_25 (and_25_out, e1, e2);
  not not_33 (not_33_out, e3);
  and and_26 (and_26_out, not_33_out, not_34_out);
  not not_34 (not_34_out, e4);
  not not_35 (not_35_out, e1);
  and and_27 (and_27_out, not_35_out, e2, not_36_out);
  not not_36 (not_36_out, e3);
  and and_28 (and_28_out, e2, not_37_out);
  not not_37 (not_37_out, e4);
  and and_29 (and_29_out, e1, not_38_out);
  not not_38 (not_38_out, e2);
  and and_30 (and_30_out, e1, e3);
  not not_39 (not_39_out, e2);
  and and_31 (and_31_out, not_39_out, e3);
  and and_32 (and_32_out, e3, not_40_out);
  not not_40 (not_40_out, e4);
  not not_41 (not_41_out, e1);
  and and_33 (and_33_out, not_41_out, e2, not_42_out);
  not not_42 (not_42_out, e3);
  and and_34 (and_34_out, e1, not_43_out);
  not not_43 (not_43_out, e2);
  and and_35 (and_35_out, e1, e4);
  or or_1 (b, and_7_out, and_8_out, and_9_out, and_10_out, and_11_out);
  or or_2 (c, and_12_out, and_13_out, and_14_out, and_15_out, and_16_out);
  or or_3 (d, and_17_out, and_18_out, and_19_out, and_20_out, and_21_out);
  or or_4 (e, and_22_out, and_23_out, and_24_out, and_25_out);
  or or_5 (f, and_26_out, and_27_out, and_28_out, and_29_out, and_30_out);
  or or_6 (g, and_31_out, and_32_out, and_33_out, and_34_out, and_35_out);
  or or_7 (a, and_1_out, and_2_out, and_3_out, and_4_out, and_5_out, and_6_out);
endmodule

module Meia_soma (
  input  x0,
  input  y0,
  output s0,
  output carry_out
);

  xor xor_1 (s0, y0, x0);
  and and_1 (carry_out, y0, x0);
endmodule

module Soma_Completa (
  input  x,
  input  y,
  input  carry_in,
  output s0,
  output carry_out
);

  wire meia_soma_1_carry_out, meia_soma_1_s0, meia_soma_2_carry_out;

  SOMADOR_Meia_soma meia_soma_1 (.x0(x), .y0(y), .s0(meia_soma_1_s0), .carry_out(meia_soma_1_carry_out));
  SOMADOR_Meia_soma meia_soma_2 (.x0(meia_soma_1_s0), .y0(carry_in), .s0(s0), .carry_out(meia_soma_2_carry_out));
  or or_1 (carry_out, meia_soma_2_carry_out, meia_soma_1_carry_out);
endmodule

module Soma_4_bits (
  input  x3,
  input  in_2,
  input  x2,
  input  x1,
  input  x0,
  input  y3,
  input  y2,
  input  y1,
  input  y0,
  output s3,
  output s2,
  output s1,
  output s0,
  output Carry_out,
  output Overflow
);

  wire soma_completa_1_carry_out, soma_completa_2_carry_out, soma_completa_3_carry_out;

  SOMADOR_Soma_Completa soma_completa_1 (
    .x(x0), .y(y0), .carry_in(in_2), .s0(s0), .carry_out(soma_completa_1_carry_out));
  SOMADOR_Soma_Completa soma_completa_2 (
    .x(x1), .y(y1), .carry_in(soma_completa_1_carry_out), .s0(s1), .carry_out(soma_completa_2_carry_out));
  SOMADOR_Soma_Completa soma_completa_3 (
    .x(y2), .y(x2), .carry_in(soma_completa_2_carry_out), .s0(s2), .carry_out(soma_completa_3_carry_out));
  SOMADOR_Soma_Completa soma_completa_4 (
    .x(x3), .y(y3), .carry_in(soma_completa_3_carry_out), .s0(s3), .carry_out(Carry_out));
  xor xor_1 (Overflow, Carry_out, soma_completa_3_carry_out);
endmodule
